// Logisim project CU1.circ as structural Verilog: 1 circuit, main circuit main
module main (
  input  C_OP_3,
  input  C_OP_2,
  input  C_OP_1,
  input  C_OP_0,
  input  S_C_2,
  input  S_C_1,
  input  S_C_0,
  output C_0,
  output C_1,
  output C_2,
  output C_3,
  output C_4,
  output C_5,
  output C_6,
  output C_7,
  output C_8,
  output C_9,
  output C_10,
  output C_11
);

  wire and_1_out, and_2_out, and_3_out, and_4_out, and_5_out, and_6_out, and_7_out, and_8_out, and_9_out,
       and_10_out, and_11_out, and_12_out, and_13_out, and_14_out, and_15_out, and_16_out, and_17_out,
       and_18_out, and_19_out, and_20_out, and_21_out, and_22_out, and_23_out, and_24_out, and_25_out,
       and_26_out, and_27_out, and_28_out, and_29_out, and_33_out, and_34_out, and_35_out, and_36_out,
       and_37_out, and_38_out, and_39_out, and_40_out, and_43_out, and_44_out, and_45_out, and_46_out,
       and_47_out, and_48_out, and_49_out, and_50_out, and_51_out, and_52_out, and_53_out, and_54_out,
       and_55_out, and_56_out, and_57_out, not_1_out, not_2_out, not_3_out, not_4_out, not_5_out, not_6_out,
       not_7_out, not_8_out, not_9_out, not_10_out, not_11_out, not_12_out, not_13_out, not_14_out,
       not_15_out, not_16_out, not_17_out, not_18_out, not_19_out, not_20_out, not_21_out, not_22_out,
       not_23_out, not_24_out, not_25_out, not_26_out, not_27_out, not_28_out, not_29_out, not_30_out,
       not_31_out, not_32_out, not_33_out, not_34_out, not_35_out, not_36_out, not_37_out, not_38_out,
       not_39_out, not_40_out, not_41_out, not_42_out, not_43_out, not_44_out, or_2_out, or_5_out, or_6_out;

  not not_1 (not_1_out, S_C_2);
  not not_2 (not_2_out, S_C_1);
  not not_3 (not_3_out, S_C_2);
  not not_4 (not_4_out, S_C_1);
  not not_5 (not_5_out, S_C_2);
  not not_6 (not_6_out, S_C_1);
  not not_7 (not_7_out, C_OP_1);
  not not_8 (not_8_out, S_C_1);
  not not_9 (not_9_out, S_C_0);
  not not_10 (not_10_out, S_C_2);
  not not_11 (not_11_out, S_C_1);
  not not_12 (not_12_out, C_OP_1);
  not not_13 (not_13_out, S_C_1);
  not not_14 (not_14_out, S_C_0);
  not not_15 (not_15_out, S_C_2);
  not not_16 (not_16_out, C_OP_1);
  not not_17 (not_17_out, S_C_1);
  not not_18 (not_18_out, S_C_2);
  not not_19 (not_19_out, C_OP_1);
  not not_20 (not_20_out, S_C_2);
  not not_21 (not_21_out, S_C_2);
  not not_22 (not_22_out, S_C_2);
  not not_23 (not_23_out, S_C_1);
  not not_24 (not_24_out, C_OP_1);
  not not_25 (not_25_out, S_C_2);
  not not_26 (not_26_out, S_C_2);
  not not_27 (not_27_out, S_C_1);
  not not_28 (not_28_out, C_OP_1);
  not not_29 (not_29_out, S_C_1);
  not not_30 (not_30_out, S_C_0);
  not not_31 (not_31_out, C_OP_0);
  and and_1 (and_1_out, not_1_out, not_2_out);
  not not_32 (not_32_out, S_C_0);
  and and_2 (and_2_out, not_3_out, not_4_out);
  and and_3 (and_3_out, C_OP_1, C_OP_0);
  and and_4 (and_4_out, and_3_out, S_C_2);
  not not_33 (not_33_out, S_C_1);
  and and_5 (and_5_out, not_33_out, not_34_out);
  not not_34 (not_34_out, S_C_0);
  and and_6 (and_6_out, not_5_out, not_6_out);
  and and_7 (and_7_out, not_7_out, S_C_2);
  and and_8 (and_8_out, not_8_out, not_9_out);
  and and_9 (and_9_out, not_10_out, not_11_out);
  and and_10 (and_10_out, not_12_out, S_C_2);
  and and_11 (and_11_out, not_13_out, not_14_out);
  not not_35 (not_35_out, S_C_2);
  and and_12 (and_12_out, not_15_out, S_C_1);
  not not_36 (not_36_out, S_C_0);
  and and_13 (and_13_out, not_16_out, S_C_2);
  and and_14 (and_14_out, not_17_out, S_C_0);
  and and_15 (and_15_out, C_OP_1, C_OP_0);
  and and_16 (and_16_out, and_15_out, S_C_2);
  not not_37 (not_37_out, S_C_1);
  and and_17 (and_17_out, not_37_out, not_38_out);
  not not_38 (not_38_out, S_C_0);
  and and_18 (and_18_out, not_18_out, S_C_1);
  not not_39 (not_39_out, S_C_0);
  and and_19 (and_19_out, not_19_out, not_20_out);
  and and_20 (and_20_out, S_C_1, S_C_0);
  and and_21 (and_21_out, C_OP_0, not_21_out);
  and and_22 (and_22_out, S_C_1, S_C_0);
  and and_23 (and_23_out, not_22_out, not_23_out);
  not not_40 (not_40_out, S_C_0);
  and and_24 (and_24_out, not_24_out, not_25_out);
  and and_25 (and_25_out, S_C_1, S_C_0);
  not not_41 (not_41_out, S_C_2);
  and and_26 (and_26_out, not_26_out, not_27_out);
  and and_27 (and_27_out, not_28_out, S_C_2);
  and and_28 (and_28_out, not_29_out, not_30_out);
  not not_42 (not_42_out, S_C_1);
  not not_43 (not_43_out, S_C_0);
  and and_29 (and_29_out, C_OP_1, not_31_out);
  not not_44 (not_44_out, S_C_2);
  and and_30 (C_0, and_1_out, not_32_out);
  and and_31 (C_1, and_2_out, S_C_0);
  and and_32 (C_2, and_4_out, and_5_out);
  and and_33 (and_33_out, and_6_out, S_C_0);
  and and_34 (and_34_out, and_7_out, and_8_out);
  and and_35 (and_35_out, and_9_out, S_C_0);
  and and_36 (and_36_out, and_10_out, and_11_out);
  and and_37 (and_37_out, C_OP_1, C_OP_0);
  and and_38 (and_38_out, not_35_out, S_C_0);
  and and_39 (and_39_out, and_12_out, not_36_out);
  and and_40 (and_40_out, and_13_out, and_14_out);
  and and_41 (C_6, and_16_out, and_17_out);
  and and_42 (C_7, and_18_out, not_39_out);
  and and_43 (and_43_out, and_19_out, and_20_out);
  and and_44 (and_44_out, and_21_out, and_22_out);
  and and_45 (and_45_out, and_23_out, not_40_out);
  and and_46 (and_46_out, and_24_out, and_25_out);
  and and_47 (and_47_out, C_OP_0, not_41_out);
  and and_48 (and_48_out, S_C_1, S_C_0);
  and and_49 (and_49_out, and_26_out, S_C_0);
  and and_50 (and_50_out, and_27_out, and_28_out);
  and and_51 (and_51_out, C_OP_0, S_C_2);
  and and_52 (and_52_out, not_42_out, not_43_out);
  and and_53 (and_53_out, and_29_out, not_44_out);
  and and_54 (and_54_out, S_C_1, S_C_0);
  or or_1 (C_3, and_33_out, and_34_out);
  or or_2 (or_2_out, and_35_out, and_36_out);
  and and_55 (and_55_out, and_37_out, and_38_out);
  or or_3 (C_5, and_39_out, and_40_out);
  or or_4 (C_8, and_43_out, and_44_out);
  or or_5 (or_5_out, and_45_out, and_46_out);
  and and_56 (and_56_out, and_47_out, and_48_out);
  or or_6 (or_6_out, and_49_out, and_50_out);
  and and_57 (and_57_out, and_51_out, and_52_out);
  and and_58 (C_11, and_53_out, and_54_out);
  or or_7 (C_4, or_2_out, and_55_out);
  or or_8 (C_9, or_5_out, and_56_out);
  or or_9 (C_10, or_6_out, and_57_out);
endmodule
