// Logisim project CU2.circ as structural Verilog: 1 circuit, main circuit main
module main (
  input  C_OP_3,
  input  C_OP_2,
  input  C_OP_1,
  input  C_OP_0,
  input  S_C_2,
  input  S_C_1,
  input  S_C_0,
  output C_12,
  output C_13,
  output C_14,
  output C_15
);

  wire and_1_out, and_2_out, and_3_out, and_4_out, and_5_out, and_6_out, and_7_out, and_8_out, and_9_out,
       and_10_out, and_12_out, and_13_out, not_1_out, not_2_out, not_3_out, not_4_out, not_5_out, not_6_out,
       not_7_out, not_8_out;

  not not_1 (not_1_out, C_OP_1);
  not not_2 (not_2_out, C_OP_0);
  not not_3 (not_3_out, C_OP_1);
  and and_1 (and_1_out, C_OP_1, C_OP_0);
  not not_4 (not_4_out, S_C_2);
  not not_5 (not_5_out, C_OP_0);
  and and_2 (and_2_out, not_1_out, not_2_out);
  not not_6 (not_6_out, S_C_1);
  and and_3 (and_3_out, not_3_out, C_OP_0);
  not not_7 (not_7_out, S_C_1);
  and and_4 (and_4_out, and_1_out, not_4_out);
  and and_5 (and_5_out, S_C_1, S_C_0);
  and and_6 (and_6_out, C_OP_1, not_5_out);
  not not_8 (not_8_out, S_C_2);
  and and_7 (and_7_out, and_2_out, S_C_2);
  and and_8 (and_8_out, not_6_out, S_C_0);
  and and_9 (and_9_out, and_3_out, S_C_2);
  and and_10 (and_10_out, not_7_out, S_C_0);
  and and_11 (C_14, and_4_out, and_5_out);
  and and_12 (and_12_out, and_6_out, not_8_out);
  and and_13 (and_13_out, S_C_1, S_C_0);
  and and_14 (C_12, and_7_out, and_8_out);
  and and_15 (C_13, and_9_out, and_10_out);
  and and_16 (C_15, and_12_out, and_13_out);
endmodule
