// Logisim project Microproccesor.circ as structural Verilog: 8 circuits, main circuit main
module main (
  input  ALU_Output_Enable,
  input  Clear,
  input  Count_Enable,
  input  Output_Enable,
  input  Output_Enable_2,
  input  in_6,
  input  [3:0] Testing_Data,
  input  in_8,
  input  in_9,
  input  [7:0] Testing_Data_2
);

  wire A_Writing_Enable, ALU_OE, B_Writing_Enable, CLK, IR_Output_Enable, IR_Writing_Enable,
       MAR_Output_Enable, MAR_Writing_Enable, MBR_Internal_Output_Enable, MBR_Output_Enable,
       MBR_Writing_Enable, OR_Output_Enable, OR_Writing_Enable, PC_Counter_Enable, PC_Counter_Output_Enable,
       Ram_Output_Enable, Ram_Writing_Enable;
  wire [2:0] Step_Counter_q;
  wire [3:0] bitselector_2_out, MAR_IN, MAR_OUT, MAR_Save, PC_OP, undriven;
  wire [7:0] A_IN, A_Output, A_Save, ALU_S, B_Output, B_Save, C_OUT, IR_OUT, IR_Save, MBR_Save, OR_Save;

  LED ID1 (.in(A_IN[0]));
  LED ID2 (.in(A_IN[1]));
  LED ID3 (.in(A_IN[2]));
  LED ID4 (.in(A_IN[3]));
  LED ID5 (.in(A_IN[4]));
  LED ID6 (.in(A_IN[5]));
  LED ID7 (.in(A_IN[6]));
  LED ID8 (.in(A_IN[7]));
  LED ED1 (.in(A_IN[0]));
  LED ED2 (.in(A_IN[1]));
  LED ED3 (.in(A_IN[2]));
  LED ED4 (.in(A_IN[3]));
  LED ED5 (.in(A_IN[4]));
  LED ED6 (.in(A_IN[5]));
  LED ED7 (.in(A_IN[6]));
  LED ED8 (.in(A_IN[7]));
  Clock Clock (.out(CLK));
  BitSelector #(.group(4)) bitselector_1 (.in(IR_OUT), .out(MAR_IN), .sel(in_8));
  Memory_Address_Register MAR (
    .Clock(CLK), .Output_Enable(MAR_Output_Enable), .Clear(Clear), .Writing_Enable(MAR_Writing_Enable),
    .Input(MAR_IN), .Output(MAR_OUT), .Save(MAR_Save));
  _8_Bits_Mem_Register Register_A (
    .Clock(CLK), .Output_Enable(Output_Enable), .Clear(Clear), .Writing_Enable(A_Writing_Enable),
    .Input(A_IN), .Output(A_Output), .Save(A_Save));
  _8_Bits_Mem_Register Register_B (
    .Clock(CLK), .Output_Enable(Output_Enable_2), .Clear(Clear), .Writing_Enable(B_Writing_Enable),
    .Input(A_IN), .Output(B_Output), .Save(B_Save));
  assign MAR_IN = PC_Counter_Output_Enable ? PC_OP : 4'bz;  // Controlled_Buffer controlled_buffer_1
  BitSelector #(.group(4)) bitselector_2 (.in(IR_Save), .out(bitselector_2_out), .sel(1'b1));
  // Probe on Step_Counter_q
  Counter #(.width(3), .max('h5)) Step_Counter (.Q(Step_Counter_q), .clk(CLK));  // open: load, D, count, carry, clr
  // Probe on A_Save
  // Probe on B_Save
  // Probe on OR_Save
  // Probe on IR_Save
  // Probe on MAR_Save
  // Probe on ALU_S
  // Probe on MBR_Save
  assign A_IN = MBR_Internal_Output_Enable ? MBR_Save : 8'bz;  // Controlled_Buffer controlled_buffer_2
  // Probe on bitselector_2_out
  Control_Unit_1 control_unit_1_1 (
    .C_OP_3(bitselector_2_out[0]), .C_OP_2(bitselector_2_out[1]), .C_OP_1(bitselector_2_out[2]),
    .C_OP_0(bitselector_2_out[3]), .S_C_2(Step_Counter_q[0]), .S_C_1(Step_Counter_q[1]),
    .S_C_0(Step_Counter_q[2]), .C_0(PC_Counter_Output_Enable), .C_1(PC_Counter_Enable),
    .C_2(Ram_Writing_Enable), .C_3(Ram_Output_Enable), .C_4(MBR_Writing_Enable),
    .C_5(MBR_Internal_Output_Enable), .C_6(MBR_Output_Enable), .C_7(IR_Writing_Enable),
    .C_8(IR_Output_Enable), .C_9(MAR_Writing_Enable), .C_10(MAR_Output_Enable), .C_11(ALU_OE));
  Control_Unit_2 control_unit_2_1 (
    .C_OP_3(undriven[0]), .C_OP_2(undriven[1]), .C_OP_1(undriven[2]), .C_OP_0(undriven[3]),
    .S_C_2(Step_Counter_q[0]), .S_C_1(Step_Counter_q[1]), .S_C_0(Step_Counter_q[2]), .C_12(A_Writing_Enable),
    .C_13(B_Writing_Enable), .C_14(OR_Output_Enable), .C_15(OR_Writing_Enable));
  assign MAR_OUT = in_6 ? Testing_Data : 4'bz;  // Controlled_Buffer controlled_buffer_3
  _8_Bits_Mem_Register Output__Register (
    .Clock(CLK), .Output_Enable(OR_Output_Enable), .Clear(Clear), .Writing_Enable(OR_Writing_Enable),
    .Input(A_IN), .Output(A_IN), .Save(OR_Save));
  _8_Bits_Mem_Register Instruction_Resgister (
    .Clock(CLK), .Output_Enable(IR_Output_Enable), .Clear(Clear), .Writing_Enable(IR_Writing_Enable),
    .Input(A_IN), .Output(IR_OUT), .Save(IR_Save));
  _8_Bits_Mem_Register MBR (
    .Clock(CLK), .Output_Enable(MBR_Output_Enable), .Clear(Clear), .Writing_Enable(MBR_Writing_Enable),
    .Input(A_IN), .Output(A_IN), .Save(MBR_Save));
  assign A_IN = in_9 ? Testing_Data_2 : 8'bz;  // Controlled_Buffer controlled_buffer_4
  Arithmatic_Logical_Unit_8_Biits ALU (
    .A(A_Save), .B(B_Save), .Output(A_IN), .Save(ALU_S), .Carry_Out(C_OUT), .Output_Enable(ALU_OE));
  // Probe on PC_OP
  Counter #(.width(4), .max('h3)) Program_Counter (
    .D(MAR_IN), .count(PC_Counter_Enable), .Q(PC_OP), .clk(CLK), .clr(Clear));  // open: load, carry
  RAM #(.addrWidth(4), .bus("separate")) ram_1 (
    .addr(MAR_OUT), .din(A_IN), .data(A_IN), .str(Ram_Writing_Enable), .clk(CLK), .ld(Ram_Output_Enable),
    .clr(Clear));  // open: sel

  // Other names for the same wires on the sheet: ALU_OUTPUT[7:0] = A_IN; B_IN[7:0] = A_IN; IR_IN[7:0] = A_IN;
  //   MBR_IN[7:0] = A_IN; MBR_OUT[7:0] = A_IN; OR_IN[7:0] = A_IN; OR_OUT[7:0] = A_IN; RAM_ED_1[7:0] = A_IN;
  //   RAM_ED_2[7:0] = A_IN; CE = Count_Enable; CLR = Clear; PC[3:0] = MAR_IN; RAM_EA[3:0] = MAR_OUT

  // Notes on the sheet:
  //   External Address Bus
  //   Internal Address Bus
  //   Internal Data Bus
  //   External Data bus
endmodule

module _1_Bit_Mem_Cell (
  input  Write_Enable,
  input  Clock,
  input  Clear,
  input  Output_Enable,
  input  Input,
  output Output,
  output Stored_Data
);

  wire and_1_out, and_2_out, not_1_out, or_1_out;

  not not_1 (not_1_out, Write_Enable);
  and and_1 (and_1_out, Stored_Data, not_1_out);
  and and_2 (and_2_out, Write_Enable, Input);
  or or_1 (or_1_out, and_1_out, and_2_out);
  D_Flip_Flop d_ff_1 (.clk(Clock), .D(or_1_out), .Q(Stored_Data), .reset(Clear));  // open: Qn, preset, en
  assign Output = Output_Enable ? Stored_Data : 1'bz;  // Controlled_Buffer controlled_buffer_1
endmodule

module _8_Bits_Mem_Register (
  input  Clock,
  input  Output_Enable,
  input  Clear,
  input  Writing_Enable,
  input  [7:0] Input,
  output [7:0] Output,
  output [7:0] Save
);

  _1_Bit_Mem_Cell u_1_bit_mem_cell_1 (
    .Write_Enable(Writing_Enable), .Input(Input[0]), .Output(Output[0]), .Stored_Data(Save[0]),
    .Clear(Clear), .Output_Enable(Output_Enable), .Clock(Clock));
  _1_Bit_Mem_Cell u_1_bit_mem_cell_2 (
    .Write_Enable(Writing_Enable), .Input(Input[1]), .Output(Output[1]), .Stored_Data(Save[1]),
    .Clear(Clear), .Output_Enable(Output_Enable), .Clock(Clock));
  _1_Bit_Mem_Cell u_1_bit_mem_cell_3 (
    .Write_Enable(Writing_Enable), .Input(Input[2]), .Output(Output[2]), .Stored_Data(Save[2]),
    .Clear(Clear), .Output_Enable(Output_Enable), .Clock(Clock));
  _1_Bit_Mem_Cell u_1_bit_mem_cell_4 (
    .Write_Enable(Writing_Enable), .Input(Input[3]), .Output(Output[3]), .Stored_Data(Save[3]),
    .Clear(Clear), .Output_Enable(Output_Enable), .Clock(Clock));
  _1_Bit_Mem_Cell u_1_bit_mem_cell_5 (
    .Write_Enable(Writing_Enable), .Input(Input[4]), .Output(Output[4]), .Stored_Data(Save[4]),
    .Clear(Clear), .Output_Enable(Output_Enable), .Clock(Clock));
  _1_Bit_Mem_Cell u_1_bit_mem_cell_6 (
    .Write_Enable(Writing_Enable), .Input(Input[5]), .Output(Output[5]), .Stored_Data(Save[5]),
    .Clear(Clear), .Output_Enable(Output_Enable), .Clock(Clock));
  _1_Bit_Mem_Cell u_1_bit_mem_cell_7 (
    .Write_Enable(Writing_Enable), .Input(Input[6]), .Output(Output[6]), .Stored_Data(Save[6]),
    .Clear(Clear), .Output_Enable(Output_Enable), .Clock(Clock));
  _1_Bit_Mem_Cell u_1_bit_mem_cell_8 (
    .Write_Enable(Writing_Enable), .Input(Input[7]), .Output(Output[7]), .Stored_Data(Save[7]),
    .Clear(Clear), .Output_Enable(Output_Enable), .Clock(Clock));
  // Probe on Output
  // Probe on Save

  // Other names for the same wires on the sheet: CLR = Clear; CT = Clock; IP1 = Input[0]; IP2 = Input[1];
  //   IP3 = Input[2]; IP4 = Input[3]; IP5 = Input[4]; IP6 = Input[5]; IP7 = Input[6]; IP8 = Input[7];
  //   OE = Output_Enable; OP1 = Output[0]; OP2 = Output[1]; OP3 = Output[2]; OP4 = Output[3]; OP5 = Output[4];
  //   OP6 = Output[5]; OP7 = Output[6]; OP8 = Output[7]; S1 = Save[0]; S2 = Save[1]; S3 = Save[2]; S4 = Save[3];
  //   S5 = Save[4]; S6 = Save[5]; S7 = Save[6]; S8 = Save[7]; WE = Writing_Enable
endmodule

module Memory_Address_Register (
  input  Clock,
  input  Output_Enable,
  input  Clear,
  input  Writing_Enable,
  input  [3:0] Input,
  output [3:0] Output,
  output [3:0] Save
);

  _1_Bit_Mem_Cell u_1_bit_mem_cell_1 (
    .Write_Enable(Writing_Enable), .Input(Input[0]), .Output(Output[0]), .Stored_Data(Save[0]),
    .Clear(Clear), .Output_Enable(Output_Enable), .Clock(Clock));
  _1_Bit_Mem_Cell u_1_bit_mem_cell_2 (
    .Write_Enable(Writing_Enable), .Input(Input[1]), .Output(Output[1]), .Stored_Data(Save[1]),
    .Clear(Clear), .Output_Enable(Output_Enable), .Clock(Clock));
  _1_Bit_Mem_Cell u_1_bit_mem_cell_3 (
    .Write_Enable(Writing_Enable), .Input(Input[2]), .Output(Output[2]), .Stored_Data(Save[2]),
    .Clear(Clear), .Output_Enable(Output_Enable), .Clock(Clock));
  _1_Bit_Mem_Cell u_1_bit_mem_cell_4 (
    .Write_Enable(Writing_Enable), .Input(Input[3]), .Output(Output[3]), .Stored_Data(Save[3]),
    .Clear(Clear), .Output_Enable(Output_Enable), .Clock(Clock));
  // Probe on Output
  // Probe on Save

  // Other names for the same wires on the sheet: CLR = Clear; CT = Clock; IP1 = Input[0]; IP2 = Input[1];
  //   IP3 = Input[2]; IP4 = Input[3]; OE = Output_Enable; OP1 = Output[0]; OP2 = Output[1]; OP3 = Output[2];
  //   OP4 = Output[3]; S1 = Save[0]; S2 = Save[1]; S3 = Save[2]; S4 = Save[3]; WE = Writing_Enable
endmodule

module Arithmatic_Logical_Unit_8_Biits (
  input  [7:0] A,
  input  [7:0] B,
  input  Output_Enable,
  output [7:0] Output,
  output [7:0] Carry_Out,
  output [7:0] Save
);

  Multiplier multiplier_1 (.a(A), .b(B), .out(Save), .cout(Carry_Out));  // open: cin
  assign Output = Output_Enable ? Save : 8'bz;  // Controlled_Buffer controlled_buffer_1
endmodule

module _7_Segment_Display (
  input  [7:0] Din,
  output [31:0] out_2
);

  ROM #(.dataWidth(32)) rom_1 (
    .addr(Din),
    .data({out_2[31:28], out_2[15:12], out_2[27:24], out_2[11:8], out_2[23:20], out_2[7:4], out_2[19:16], out_2[3:0]}));  // open: sel

  // Notes on the sheet:
  //   contents of rom_1 (hex, n*v repeats v):
  //   e7 21 cb 6b 2d 6e ee 23 ef 2f 21e7 2121 21cb 216b 212d 216e 21ee 2123 21ef 212f cbe7 cb21 cbcb cb6b
  //   cb2d cb6e cbee cb23 cbef cb2f 6be7 6b21 6bcb 6b6b 6b2d 6b6e 6bee 6b23 6bef 6b2f 2de7 2d21 2dcb 2d6b
  //   2d2d 2d6e 2dee 2d23 2def 2d2f 6ee7 6e21 6ecb 6e6b 6e2d 6e6e 6eee 6e23 6eef 6e2f eee7 ee21 eecb ee6b
  //   ee2d ee6e eeee ee23 eeef ee2f 23e7 2321 23cb 236b 232d 236e 23ee 2323 23ef 232f efe7 ef21 efcb ef6b
  //   ef2d ef6e efee ef23 efef ef2f 2fe7 2f21 2fcb 2f6b 2f2d 2f6e 2fee 2f23 2fef 2f2f 21e7e7 21e721 21e7cb
  //   21e76b 21e72d 21e76e 21e7ee 21e723 21e7ef 21e72f 2121e7 212121 2121cb 21216b 21212d 21216e 2121ee
  //   212123 2121ef 21212f 21cbe7 21cb21 21cbcb 21cb6b 21cb2d 21cb6e 21cbee 21cb23 21cbef 21cb2f 216be7
  //   216b21 216bcb 216b6b 216b2d 216b6e 216bee 216b23 216bef 216b2f 212de7 212d21 212dcb 212d6b 212d2d
  //   212d6e 212dee 212d23 212def 212d2f 216ee7 216e21 216ecb 216e6b 216e2d 216e6e 216eee 216e23 216eef
  //   216e2f 21eee7 21ee21 21eecb 21ee6b 21ee2d 21ee6e 21eeee 21ee23 21eeef 21ee2f 2123e7 212321 2123cb
  //   21236b 21232d 21236e 2123ee 212323 2123ef 21232f 21efe7 21ef21 21efcb 21ef6b 21ef2d 21ef6e 21efee
  //   21ef23 21efef 21ef2f 212fe7 212f21 212fcb 212f6b 212f2d 212f6e 212fee 212f23 212fef 212f2f cbe7e7
  //   cbe721 cbe7cb cbe76b cbe72d cbe76e cbe7ee cbe723 cbe7ef cbe72f cb21e7 cb2121 cb21cb cb216b cb212d
  //   cb216e cb21ee cb2123 cb21ef cb212f cbcbe7 cbcb21 cbcbcb cbcb6b cbcb2d cbcb6e cbcbee cbcb23 cbcbef
  //   cbcb2f cb6be7 cb6b21 cb6bcb cb6b6b cb6b2d cb6b6e cb6bee cb6b23 cb6bef cb6b2f cb2de7 cb2d21 cb2dcb
  //   cb2d6b cb2d2d cb2d6e cb2dee cb2d23 cb2def cb2d2f cb6ee7 cb6e21 cb6ecb cb6e6b cb6e2d cb6e6e
endmodule

module Control_Unit_1 (
  input  C_OP_3,
  input  C_OP_2,
  input  C_OP_1,
  input  C_OP_0,
  input  S_C_2,
  input  S_C_1,
  input  S_C_0,
  output C_0,
  output C_1,
  output C_2,
  output C_3,
  output C_4,
  output C_5,
  output C_6,
  output C_7,
  output C_8,
  output C_9,
  output C_10,
  output C_11
);

  wire and_1_out, and_2_out, and_3_out, and_4_out, and_5_out, and_6_out, and_7_out, and_8_out, and_9_out,
       and_10_out, and_11_out, and_12_out, and_13_out, and_14_out, and_15_out, and_16_out, and_17_out,
       and_18_out, and_19_out, and_20_out, and_21_out, and_22_out, and_23_out, and_24_out, and_25_out,
       and_26_out, and_27_out, and_28_out, and_29_out, and_33_out, and_34_out, and_35_out, and_36_out,
       and_37_out, and_38_out, and_39_out, and_40_out, and_43_out, and_44_out, and_45_out, and_46_out,
       and_47_out, and_48_out, and_49_out, and_50_out, and_51_out, and_52_out, and_53_out, and_54_out,
       and_55_out, and_56_out, and_57_out, not_1_out, not_2_out, not_3_out, not_4_out, not_5_out, not_6_out,
       not_7_out, not_8_out, not_9_out, not_10_out, not_11_out, not_12_out, not_13_out, not_14_out,
       not_15_out, not_16_out, not_17_out, not_18_out, not_19_out, not_20_out, not_21_out, not_22_out,
       not_23_out, not_24_out, not_25_out, not_26_out, not_27_out, not_28_out, not_29_out, not_30_out,
       not_31_out, not_32_out, not_33_out, not_34_out, not_35_out, not_36_out, not_37_out, not_38_out,
       not_39_out, not_40_out, not_41_out, not_42_out, not_43_out, not_44_out, or_2_out, or_5_out, or_6_out;

  not not_1 (not_1_out, S_C_2);
  not not_2 (not_2_out, S_C_1);
  not not_3 (not_3_out, S_C_2);
  not not_4 (not_4_out, S_C_1);
  not not_5 (not_5_out, S_C_2);
  not not_6 (not_6_out, S_C_1);
  not not_7 (not_7_out, C_OP_1);
  not not_8 (not_8_out, S_C_1);
  not not_9 (not_9_out, S_C_0);
  not not_10 (not_10_out, S_C_2);
  not not_11 (not_11_out, S_C_1);
  not not_12 (not_12_out, C_OP_1);
  not not_13 (not_13_out, S_C_1);
  not not_14 (not_14_out, S_C_0);
  not not_15 (not_15_out, S_C_2);
  not not_16 (not_16_out, C_OP_1);
  not not_17 (not_17_out, S_C_1);
  not not_18 (not_18_out, S_C_2);
  not not_19 (not_19_out, C_OP_1);
  not not_20 (not_20_out, S_C_2);
  not not_21 (not_21_out, S_C_2);
  not not_22 (not_22_out, S_C_2);
  not not_23 (not_23_out, S_C_1);
  not not_24 (not_24_out, C_OP_1);
  not not_25 (not_25_out, S_C_2);
  not not_26 (not_26_out, S_C_2);
  not not_27 (not_27_out, S_C_1);
  not not_28 (not_28_out, C_OP_1);
  not not_29 (not_29_out, S_C_1);
  not not_30 (not_30_out, S_C_0);
  not not_31 (not_31_out, C_OP_0);
  and and_1 (and_1_out, not_1_out, not_2_out);
  not not_32 (not_32_out, S_C_0);
  and and_2 (and_2_out, not_3_out, not_4_out);
  and and_3 (and_3_out, C_OP_1, C_OP_0);
  and and_4 (and_4_out, and_3_out, S_C_2);
  not not_33 (not_33_out, S_C_1);
  and and_5 (and_5_out, not_33_out, not_34_out);
  not not_34 (not_34_out, S_C_0);
  and and_6 (and_6_out, not_5_out, not_6_out);
  and and_7 (and_7_out, not_7_out, S_C_2);
  and and_8 (and_8_out, not_8_out, not_9_out);
  and and_9 (and_9_out, not_10_out, not_11_out);
  and and_10 (and_10_out, not_12_out, S_C_2);
  and and_11 (and_11_out, not_13_out, not_14_out);
  not not_35 (not_35_out, S_C_2);
  and and_12 (and_12_out, not_15_out, S_C_1);
  not not_36 (not_36_out, S_C_0);
  and and_13 (and_13_out, not_16_out, S_C_2);
  and and_14 (and_14_out, not_17_out, S_C_0);
  and and_15 (and_15_out, C_OP_1, C_OP_0);
  and and_16 (and_16_out, and_15_out, S_C_2);
  not not_37 (not_37_out, S_C_1);
  and and_17 (and_17_out, not_37_out, not_38_out);
  not not_38 (not_38_out, S_C_0);
  and and_18 (and_18_out, not_18_out, S_C_1);
  not not_39 (not_39_out, S_C_0);
  and and_19 (and_19_out, not_19_out, not_20_out);
  and and_20 (and_20_out, S_C_1, S_C_0);
  and and_21 (and_21_out, C_OP_0, not_21_out);
  and and_22 (and_22_out, S_C_1, S_C_0);
  and and_23 (and_23_out, not_22_out, not_23_out);
  not not_40 (not_40_out, S_C_0);
  and and_24 (and_24_out, not_24_out, not_25_out);
  and and_25 (and_25_out, S_C_1, S_C_0);
  not not_41 (not_41_out, S_C_2);
  and and_26 (and_26_out, not_26_out, not_27_out);
  and and_27 (and_27_out, not_28_out, S_C_2);
  and and_28 (and_28_out, not_29_out, not_30_out);
  not not_42 (not_42_out, S_C_1);
  not not_43 (not_43_out, S_C_0);
  and and_29 (and_29_out, C_OP_1, not_31_out);
  not not_44 (not_44_out, S_C_2);
  and and_30 (C_0, and_1_out, not_32_out);
  and and_31 (C_1, and_2_out, S_C_0);
  and and_32 (C_2, and_4_out, and_5_out);
  and and_33 (and_33_out, and_6_out, S_C_0);
  and and_34 (and_34_out, and_7_out, and_8_out);
  and and_35 (and_35_out, and_9_out, S_C_0);
  and and_36 (and_36_out, and_10_out, and_11_out);
  and and_37 (and_37_out, C_OP_1, C_OP_0);
  and and_38 (and_38_out, not_35_out, S_C_0);
  and and_39 (and_39_out, and_12_out, not_36_out);
  and and_40 (and_40_out, and_13_out, and_14_out);
  and and_41 (C_6, and_16_out, and_17_out);
  and and_42 (C_7, and_18_out, not_39_out);
  and and_43 (and_43_out, and_19_out, and_20_out);
  and and_44 (and_44_out, and_21_out, and_22_out);
  and and_45 (and_45_out, and_23_out, not_40_out);
  and and_46 (and_46_out, and_24_out, and_25_out);
  and and_47 (and_47_out, C_OP_0, not_41_out);
  and and_48 (and_48_out, S_C_1, S_C_0);
  and and_49 (and_49_out, and_26_out, S_C_0);
  and and_50 (and_50_out, and_27_out, and_28_out);
  and and_51 (and_51_out, C_OP_0, S_C_2);
  and and_52 (and_52_out, not_42_out, not_43_out);
  and and_53 (and_53_out, and_29_out, not_44_out);
  and and_54 (and_54_out, S_C_1, S_C_0);
  or or_1 (C_3, and_33_out, and_34_out);
  or or_2 (or_2_out, and_35_out, and_36_out);
  and and_55 (and_55_out, and_37_out, and_38_out);
  or or_3 (C_5, and_39_out, and_40_out);
  or or_4 (C_8, and_43_out, and_44_out);
  or or_5 (or_5_out, and_45_out, and_46_out);
  and and_56 (and_56_out, and_47_out, and_48_out);
  or or_6 (or_6_out, and_49_out, and_50_out);
  and and_57 (and_57_out, and_51_out, and_52_out);
  and and_58 (C_11, and_53_out, and_54_out);
  or or_7 (C_4, or_2_out, and_55_out);
  or or_8 (C_9, or_5_out, and_56_out);
  or or_9 (C_10, or_6_out, and_57_out);
endmodule

module Control_Unit_2 (
  input  C_OP_3,
  input  C_OP_2,
  input  C_OP_1,
  input  C_OP_0,
  input  S_C_2,
  input  S_C_1,
  input  S_C_0,
  output C_12,
  output C_13,
  output C_14,
  output C_15
);

  wire and_1_out, and_2_out, and_3_out, and_4_out, and_5_out, and_6_out, and_7_out, and_8_out, and_9_out,
       and_10_out, and_12_out, and_13_out, not_1_out, not_2_out, not_3_out, not_4_out, not_5_out, not_6_out,
       not_7_out, not_8_out;

  not not_1 (not_1_out, C_OP_1);
  not not_2 (not_2_out, C_OP_0);
  not not_3 (not_3_out, C_OP_1);
  and and_1 (and_1_out, C_OP_1, C_OP_0);
  not not_4 (not_4_out, S_C_2);
  not not_5 (not_5_out, C_OP_0);
  and and_2 (and_2_out, not_1_out, not_2_out);
  not not_6 (not_6_out, S_C_1);
  and and_3 (and_3_out, not_3_out, C_OP_0);
  not not_7 (not_7_out, S_C_1);
  and and_4 (and_4_out, and_1_out, not_4_out);
  and and_5 (and_5_out, S_C_1, S_C_0);
  and and_6 (and_6_out, C_OP_1, not_5_out);
  not not_8 (not_8_out, S_C_2);
  and and_7 (and_7_out, and_2_out, S_C_2);
  and and_8 (and_8_out, not_6_out, S_C_0);
  and and_9 (and_9_out, and_3_out, S_C_2);
  and and_10 (and_10_out, not_7_out, S_C_0);
  and and_11 (C_14, and_4_out, and_5_out);
  and and_12 (and_12_out, and_6_out, not_8_out);
  and and_13 (and_13_out, S_C_1, S_C_0);
  and and_14 (C_12, and_7_out, and_8_out);
  and and_15 (C_13, and_9_out, and_10_out);
  and and_16 (C_15, and_12_out, and_13_out);
endmodule
